# Fritzing sketch Sketch (saved by Fritzing 0.9.3b)
breadboards: 2

parts:
  Ameba1 = Ameba
  M1 = MakerFocus MAX30102
  Part1 = Adafruit PCF8523 RTC [part_number="Adafruit #3295"]  # not connected
  Part2 = Adafruit SGP30 Gas Sensor

nets:
  GND: Ameba1.GND, M1.GND, Part2.GND
  N1: M1.SCL, Part2.SCL
  N2: M1.SDA, Part2.SDA
  VIN: M1.VIN, Part2.VIN

custom parts:
  Ameba: Ameba EVB
  MakerFocus MAX30102: Oximeter module using the MAX30102 chip. As usual, if you want the mounting holes in pcb, you need to drag a hole over the pad in silkscreen to actually drill the hole (by default they are not drilled)
  Adafruit PCF8523 RTC: This is a great battery-backed real time clock (RTC) that allows your microcontroller project to keep track of time even if it is reprogrammed, or if the power is lost. Perfect for datalogging, clock-building, time stamping, timers and alarms, etc. Equipped with PCF8523 RTC - it can run from 3.3V or 5V power & logic! Works great with an Arduino using our RTC library, with CircuitPython or with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
